# Fritzing sketch flash-trigger (saved by Fritzing 0.9.3b)
breadboards: 1

parts:
  U1 = NodeMCU V3.0
  Arduino_Pro_Mini_3_3V = Arduino Pro Mini (3.3V)

nets:
  3V3: U1.3V3, Arduino_Pro_Mini_3_3V.VCC
  N1: U1.GND#6, U1.GND#13, U1.GND#16, U1.GND#33, Arduino_Pro_Mini_3_3V.GND
  N2: U1.D5, Arduino_Pro_Mini_3_3V.RESET
  N3: U1.D7, Arduino_Pro_Mini_3_3V.TXO
  N4: U1.D8, Arduino_Pro_Mini_3_3V.RXI

custom parts:
  NodeMCU V3.0: ESP8266 based NodeMCU
